// Logisim project nfet.circ as structural Verilog: 3 circuits, main circuit g_nor
module g_rsff (
  input  reset,
  input  set,
  output q,
  output nq
);

  g_nor g_nor_1 (.a(reset), .b(nq), .x(q));
  g_nor g_nor_2 (.a(q), .b(set), .x(nq));
endmodule

module g_nor (
  input  a,
  input  b,
  output x
);

  nfet nfet_1 (.gate(a), .a_in(1'b0), .b_in(1'b1), .a_out(x), .b_out(x));
  nfet nfet_2 (.gate(b), .a_in(1'b0), .b_in(1'b1), .a_out(x), .b_out(x));
  Pull_Resistor #(.pull(1)) pull_resistor_1 (.node(x));

  // Notes on the sheet:
  //   nor
endmodule

module nfet (
  input  gate,
  input  a_in,
  input  b_in,
  output a_out,
  output b_out
);

  wire d_ff_1_q, d_ff_2_q, multiplexer_1_out, multiplexer_2_out, not_1_out;

  Multiplexer multiplexer_1 (.in0(1'b0), .in1(1'b1), .out(multiplexer_1_out), .sel(a_in));
  D_Flip_Flop #(.trigger("high")) d_ff_1 (.clk(1'b1), .D(gate), .Q(d_ff_1_q));  // open: Qn, preset, reset
  Multiplexer multiplexer_2 (.in0(1'b0), .in1(multiplexer_1_out), .out(multiplexer_2_out), .sel(b_in));
  D_Flip_Flop #(.trigger("high")) d_ff_2 (.clk(1'b1), .D(multiplexer_2_out), .Q(d_ff_2_q));  // open: Qn, preset, reset
  not not_1 (not_1_out, d_ff_1_q);
  // Transmission_Gate transmission_1: pin names not known; wires that end beside it: d_ff_2_q, not_1_out, d_ff_1_q, a_out

  assign b_out = a_out;
endmodule
